// Logisim project N-1.circ as structural Verilog: 5 circuits, main circuit Simple_PC
module NEUTROSER_N1 (
  input  CLK,
  input  RST,
  input  DI0,
  input  DI1,
  input  DI2,
  input  DI3,
  input  DI4,
  input  DI5,
  input  DI6,
  input  DI7,
  input  DI8,
  input  DI9,
  input  DI10,
  input  DI11,
  input  DI12,
  input  DI13,
  input  DI14,
  input  DI15,
  output WE,
  output MC0,
  output MC1,
  output MC2,
  output SYNC,
  output MC3,
  output MC4,
  output MC5,
  output MC6,
  output MC7,
  output DO0,
  output DO1,
  output DO2,
  output DO3,
  output DO4,
  output DO5,
  output DO6,
  output DO7,
  output DO8,
  output DO9,
  output DO10,
  output DO11,
  output DO12,
  output DO13,
  output DO14,
  output DO15
);

  wire and_3_out, and_4_out, and_5_out, and_6_out, and_7_out, and_8_out, and_9_out, and_10_out, and_11_out,
       and_12_out, and_13_out, and_14_out, CHANGE, cmdclk, cswitch, DIV, INV, JUMP, LAND, LOAD, LOR, LXOR,
       MUL, not_1_out, not_2_out, or_2_out, SHL, SHR, SUB, SUM, WRITE;
  wire [4:0] bit_extender_1_out;
  wire [7:0] ADDR, counter_1_q, register_3_q;
  wire [15:0] multiplexer_2_out, nealu_1_lout, PRAM;

  not not_1 (not_1_out, JUMP);
  Counter #(.ongoal("stay"), .trigger("falling")) counter_1 (
    .load(JUMP), .D({DI7, DI6, DI5, DI4, DI3, DI2, DI1, DI0}), .count(not_1_out), .Q(counter_1_q),
    .clk(cswitch), .clr(RST));  // open: carry, up
  or or_1 (SYNC, CLK, RST);
  Multiplexer #(.width(8)) multiplexer_1 (
    .in0(counter_1_q), .in1(ADDR), .out({MC7, MC6, MC5, MC4, MC3, MC2, MC1, MC0}), .sel(cswitch));
  and and_1 (WE, cswitch, WRITE);
  Counter #(.max('h1), .width(1)) counter_2 (.Q(cswitch), .clk(CLK), .clr(RST));  // open: load, D, count, carry, up
  Register #(.trigger("falling"), .width(16)) register_1 (
    .D({DI15, DI14, DI13, DI12, DI11, DI10, DI9, DI8, DI7, DI6, DI5, DI4, DI3, DI2, DI1, DI0}), .Q(PRAM),
    .clk(cswitch), .clr(RST));  // open: en
  Register register_2 (.D({DI7, DI6, DI5, DI4, DI3, DI2, DI1, DI0}), .Q(ADDR), .clk(cswitch), .clr(RST));  // open: en
  Register register_3 (
    .D({DI15, DI14, DI13, DI12, DI11, DI10, DI9, DI8}), .Q(register_3_q), .clk(cswitch), .clr(RST));  // open: en
  Decoder #(.select(5)) decoder_1 (
    .out1(LOAD), .out2(JUMP), .out3(SUM), .out4(SUB), .out5(MUL), .out6(DIV), .out7(INV), .out8(LAND),
    .out9(LOR), .out10(LXOR), .out11(WRITE), .out12(CHANGE), .out13(SHR), .out14(SHL),
    .sel(bit_extender_1_out));  // open: out0, out15, out16, out17, out18, out19, out20, out21, out22, out23, out24, out25, out26, out27, out28, out29, out30, out31, en
  Bit_Extender #(.out_width(5)) bit_extender_1 (.in(register_3_q), .out(bit_extender_1_out));
  not not_2 (not_2_out, cswitch);
  and and_2 (cmdclk, not_2_out, CLK);
  NeALU nealu_1 (
    .LOUT(nealu_1_lout), .MUL(MUL), .LAND(LAND), .LOR(LOR), .LXOR(LXOR), .DIV(DIV), .INV(INV), .SHR(SHR),
    .SHL(SHL), .SUM(SUM), .SUB(SUB), .B(PRAM),
    .A({DO15, DO14, DO13, DO12, DO11, DO10, DO9, DO8, DO7, DO6, DO5, DO4, DO3, DO2, DO1, DO0}));
  and and_3 (and_3_out, SHL, cmdclk);
  and and_4 (and_4_out, SHR, cmdclk);
  and and_5 (and_5_out, INV, cmdclk);
  and and_6 (and_6_out, DIV, cmdclk);
  and and_7 (and_7_out, MUL, cmdclk);
  and and_8 (and_8_out, SUB, cmdclk);
  and and_9 (and_9_out, SUM, cmdclk);
  and and_10 (and_10_out, LAND, cmdclk);
  and and_11 (and_11_out, LOR, cmdclk);
  and and_12 (and_12_out, LXOR, cmdclk);
  and and_13 (and_13_out, LOAD, cmdclk);
  Multiplexer #(.width(16)) multiplexer_2 (.in0(nealu_1_lout), .in1(PRAM), .out(multiplexer_2_out), .sel(LOAD));
  or or_2 (or_2_out, and_3_out, and_4_out, and_5_out, and_6_out, and_7_out, and_8_out, and_9_out, and_10_out, and_11_out, and_12_out, and_13_out);
  and and_14 (and_14_out, cmdclk, CHANGE);
  NeRegs neregs_1 (
    .ROUT({DO15, DO14, DO13, DO12, DO11, DO10, DO9, DO8, DO7, DO6, DO5, DO4, DO3, DO2, DO1, DO0}),
    .LOCK(not_2_out), .ADDRCLK(and_14_out), .ADDR(PRAM), .RST(RST), .DATA(multiplexer_2_out), .CLK(or_2_out));

  // Other names for the same wires on the sheet: CDDR[7:0] = {DI7, DI6, DI5, DI4, DI3, DI2, DI1, DI0};
  //   PCOUNTER[7:0] = {MC7, MC6, MC5, MC4, MC3, MC2, MC1, MC0}; RCLK = CLK;
  //   regis[15:0] = {DO15, DO14, DO13, DO12, DO11, DO10, DO9, DO8, DO7, DO6, DO5, DO4, DO3, DO2, DO1, DO0}

  // Notes on the sheet:
  //   LOAD 01
  //   JUMP 02
  //   SUM 03
  //   SUB 04
  //   MUL 05
  //   DIV 06
  //   INV 07
  //   AND 08
  //   OR 09
  //   XOR 0a
  //   WRITE 0b
  //   CHANGE 0c
  //   SHR 0d
  //   SHL 0e
endmodule

module NeALU (
  input  [15:0] A,
  input  [15:0] B,
  input  SUM,
  input  SUB,
  input  MUL,
  input  LAND,
  input  LOR,
  input  LXOR,
  input  DIV,
  input  INV,
  input  SHR,
  input  SHL,
  output [15:0] LOUT
);

  wire nor_1_out;
  wire [3:0] bit_extender_1_out, bit_extender_2_out;
  wire [15:0] adder_1_out, and_1_out, divider_1_out, multiplier_1_out, negator_1_out, or_1_out,
       shifter_1_out, shifter_2_out, subtractor_1_out, xor_1_out;

  Bit_Extender #(.in_width(16), .out_width(4)) bit_extender_1 (.in(B), .out(bit_extender_1_out));
  Bit_Extender #(.in_width(16), .out_width(4)) bit_extender_2 (.in(B), .out(bit_extender_2_out));
  assign LOUT = SHR ? shifter_1_out : 16'bz;  // Controlled_Buffer controlled_buffer_1
  Shifter #(.shift("lr"), .width(16)) shifter_1 (.in(A), .\dist (bit_extender_1_out), .out(shifter_1_out));
  assign LOUT = SHL ? shifter_2_out : 16'bz;  // Controlled_Buffer controlled_buffer_2
  Shifter #(.width(16)) shifter_2 (.in(A), .\dist (bit_extender_2_out), .out(shifter_2_out));
  assign LOUT = INV ? negator_1_out : 16'bz;  // Controlled_Buffer controlled_buffer_3
  Negator #(.width(16)) negator_1 (.in(B), .out(negator_1_out));
  assign LOUT = DIV ? divider_1_out : 16'bz;  // Controlled_Buffer controlled_buffer_4
  Divider #(.mode("twosComplement"), .width(16)) divider_1 (.a(A), .b(B), .out(divider_1_out));  // open: upper, rem
  assign LOUT = SUM ? adder_1_out : 16'bz;  // Controlled_Buffer controlled_buffer_5
  Adder #(.width(16)) adder_1 (.a(A), .b(B), .out(adder_1_out));  // open: cin, cout
  assign LOUT = SUB ? subtractor_1_out : 16'bz;  // Controlled_Buffer controlled_buffer_6
  Subtractor #(.width(16)) subtractor_1 (.a(A), .b(B), .out(subtractor_1_out));  // open: bin, bout
  assign LOUT = MUL ? multiplier_1_out : 16'bz;  // Controlled_Buffer controlled_buffer_7
  Multiplier #(.width(16)) multiplier_1 (.a(A), .b(B), .out(multiplier_1_out));  // open: cin, cout
  assign and_1_out = A & B;  // AND_Gate and_1, 16 bits wide
  assign LOUT = LAND ? and_1_out : 16'bz;  // Controlled_Buffer controlled_buffer_8
  assign or_1_out = A | B;  // OR_Gate or_1, 16 bits wide
  assign LOUT = LOR ? or_1_out : 16'bz;  // Controlled_Buffer controlled_buffer_9
  assign xor_1_out = A ^ B;  // XOR_Gate xor_1, 16 bits wide
  assign LOUT = LXOR ? xor_1_out : 16'bz;  // Controlled_Buffer controlled_buffer_10
  assign LOUT = nor_1_out ? B : 16'bz;  // Controlled_Buffer controlled_buffer_11
  nor nor_1 (nor_1_out, LAND, LXOR, LOR, SUB, MUL, SUM, DIV, INV, SHR, SHL);
endmodule

module NeRegs (
  input  [15:0] DATA,
  input  RST,
  input  [15:0] ADDR,
  input  LOCK,
  input  ADDRCLK,
  input  CLK,
  output [15:0] ROUT
);

  wire decoder_1_out0, decoder_1_out1, decoder_1_out2, decoder_1_out3, decoder_1_out4, decoder_1_out5,
       decoder_1_out6, decoder_1_out7, decoder_1_out8, decoder_1_out9, decoder_1_out10, decoder_1_out11,
       decoder_1_out12, decoder_1_out13, decoder_1_out14, decoder_1_out15;
  wire [3:0] bit_extender_1_out;
  wire [15:0] demultiplexer_1_out0, demultiplexer_1_out1, demultiplexer_1_out2, demultiplexer_1_out3,
       demultiplexer_1_out4, demultiplexer_1_out5, demultiplexer_1_out6, demultiplexer_1_out7,
       demultiplexer_1_out8, demultiplexer_1_out9, demultiplexer_1_out10, demultiplexer_1_out11,
       demultiplexer_1_out12, demultiplexer_1_out13, demultiplexer_1_out14, demultiplexer_1_out15,
       register_1_q, register_2_q, register_3_q, register_4_q, register_5_q, register_6_q, register_7_q,
       register_8_q, register_9_q, register_10_q, register_11_q, register_12_q, register_13_q, register_14_q,
       register_15_q, register_16_q, register_17_q;

  Register #(.trigger("falling"), .width(16)) register_1 (
    .D(ADDR), .en(LOCK), .Q(register_1_q), .clk(ADDRCLK), .clr(RST));
  Demultiplexer #(.select(4), .width(16)) demultiplexer_1 (
    .out0(demultiplexer_1_out0), .out1(demultiplexer_1_out1), .out2(demultiplexer_1_out2),
    .out3(demultiplexer_1_out3), .out4(demultiplexer_1_out4), .out5(demultiplexer_1_out5),
    .out6(demultiplexer_1_out6), .out7(demultiplexer_1_out7), .out8(demultiplexer_1_out8),
    .out9(demultiplexer_1_out9), .out10(demultiplexer_1_out10), .out11(demultiplexer_1_out11),
    .out12(demultiplexer_1_out12), .out13(demultiplexer_1_out13), .out14(demultiplexer_1_out14),
    .out15(demultiplexer_1_out15), .in(DATA), .sel(bit_extender_1_out));
  Bit_Extender #(.in_width(16), .out_width(4)) bit_extender_1 (.in(register_1_q), .out(bit_extender_1_out));
  Decoder #(.select(4)) decoder_1 (
    .out0(decoder_1_out0), .out1(decoder_1_out1), .out2(decoder_1_out2), .out3(decoder_1_out3),
    .out4(decoder_1_out4), .out5(decoder_1_out5), .out6(decoder_1_out6), .out7(decoder_1_out7),
    .out8(decoder_1_out8), .out9(decoder_1_out9), .out10(decoder_1_out10), .out11(decoder_1_out11),
    .out12(decoder_1_out12), .out13(decoder_1_out13), .out14(decoder_1_out14), .out15(decoder_1_out15),
    .sel(bit_extender_1_out), .en(CLK));
  Register #(.trigger("falling"), .width(16)) register_2 (
    .D(demultiplexer_1_out0), .en(LOCK), .Q(register_2_q), .clk(decoder_1_out0), .clr(RST));
  Register #(.trigger("falling"), .width(16)) register_3 (
    .D(demultiplexer_1_out1), .en(LOCK), .Q(register_3_q), .clk(decoder_1_out1), .clr(RST));
  Register #(.trigger("falling"), .width(16)) register_4 (
    .D(demultiplexer_1_out2), .en(LOCK), .Q(register_4_q), .clk(decoder_1_out2), .clr(RST));
  Register #(.trigger("falling"), .width(16)) register_5 (
    .D(demultiplexer_1_out3), .en(LOCK), .Q(register_5_q), .clk(decoder_1_out3), .clr(RST));
  Register #(.trigger("falling"), .width(16)) register_6 (
    .D(demultiplexer_1_out4), .en(LOCK), .Q(register_6_q), .clk(decoder_1_out4), .clr(RST));
  Register #(.trigger("falling"), .width(16)) register_7 (
    .D(demultiplexer_1_out5), .en(LOCK), .Q(register_7_q), .clk(decoder_1_out5), .clr(RST));
  Register #(.trigger("falling"), .width(16)) register_8 (
    .D(demultiplexer_1_out6), .en(LOCK), .Q(register_8_q), .clk(decoder_1_out6), .clr(RST));
  Register #(.trigger("falling"), .width(16)) register_9 (
    .D(demultiplexer_1_out7), .en(LOCK), .Q(register_9_q), .clk(decoder_1_out7), .clr(RST));
  Register #(.trigger("falling"), .width(16)) register_10 (
    .D(demultiplexer_1_out8), .en(LOCK), .Q(register_10_q), .clk(decoder_1_out8), .clr(RST));
  Register #(.trigger("falling"), .width(16)) register_11 (
    .D(demultiplexer_1_out9), .en(LOCK), .Q(register_11_q), .clk(decoder_1_out9), .clr(RST));
  Register #(.trigger("falling"), .width(16)) register_12 (
    .D(demultiplexer_1_out10), .en(LOCK), .Q(register_12_q), .clk(decoder_1_out10), .clr(RST));
  Register #(.trigger("falling"), .width(16)) register_13 (
    .D(demultiplexer_1_out11), .en(LOCK), .Q(register_13_q), .clk(decoder_1_out11), .clr(RST));
  Register #(.trigger("falling"), .width(16)) register_14 (
    .D(demultiplexer_1_out12), .en(LOCK), .Q(register_14_q), .clk(decoder_1_out12), .clr(RST));
  Register #(.trigger("falling"), .width(16)) register_15 (
    .D(demultiplexer_1_out13), .en(LOCK), .Q(register_15_q), .clk(decoder_1_out13), .clr(RST));
  Register #(.trigger("falling"), .width(16)) register_16 (
    .D(demultiplexer_1_out14), .en(LOCK), .Q(register_16_q), .clk(decoder_1_out14), .clr(RST));
  Register #(.trigger("falling"), .width(16)) register_17 (
    .D(demultiplexer_1_out15), .en(LOCK), .Q(register_17_q), .clk(decoder_1_out15), .clr(RST));
  Multiplexer #(.select(4), .width(16)) multiplexer_1 (
    .in0(register_2_q), .in1(register_3_q), .in2(register_4_q), .in3(register_5_q), .in4(register_6_q),
    .in5(register_7_q), .in6(register_8_q), .in7(register_9_q), .in8(register_10_q), .in9(register_11_q),
    .in10(register_12_q), .in11(register_13_q), .in12(register_14_q), .in13(register_15_q),
    .in14(register_16_q), .in15(register_17_q), .out(ROUT), .sel(bit_extender_1_out));
endmodule

module Simple_PC (
);

  wire and_2_out, button_1_out, CLK, clock_1_out, controlled_buffer_2_out, LWE, neutroser_n1_1_sync,
       neutroser_n1_1_we, not_1_out, not_2_out, not_3_out, not_4_out, not_5_out, or_2_out, ram_loader_1_sync,
       RST, RSTProc, rsync, st0, stsy;
  wire [1:0] counter_1_q;
  wire [7:0] controlled_buffer_1_out, MC, ram_loader_1_mc;
  wire [15:0] controlled_buffer_6_out, DI, ram_loader_1_dout, rom_1_data, ROUT;

  Counter #(.max('h2), .ongoal("stay"), .width(2)) counter_1 (
    .Q(counter_1_q), .clk(st0), .clr(RST));  // open: load, D, count, carry, up
  not not_1 (not_1_out, LWE);
  and and_1 (st0, CLK, not_1_out);
  and and_2 (and_2_out, CLK, counter_1_q[1]);
  or or_1 (rsync, st0, stsy);
  or or_2 (or_2_out, RST, RSTProc);
  ROM #(.dataWidth(16)) rom_1 (.addr(ram_loader_1_mc), .data(rom_1_data));
  not not_2 (not_2_out, LWE);
  assign controlled_buffer_1_out = not_2_out ? MC : 8'bz;  // Controlled_Buffer controlled_buffer_1
  assign controlled_buffer_2_out = not_3_out ? neutroser_n1_1_we : 1'bz;  // Controlled_Buffer controlled_buffer_2
  not not_3 (not_3_out, LWE);
  NEUTROSER_N1 neutroser_n1_1 (
    .SYNC(neutroser_n1_1_sync), .WE(neutroser_n1_1_we), .DO8(ROUT[8]), .DO9(ROUT[9]), .DO10(ROUT[10]),
    .DO11(ROUT[11]), .DO12(ROUT[12]), .DO13(ROUT[13]), .DO14(ROUT[14]), .DO15(ROUT[15]), .DO0(ROUT[0]),
    .DO1(ROUT[1]), .DO2(ROUT[2]), .DO3(ROUT[3]), .DO4(ROUT[4]), .DO5(ROUT[5]), .DO6(ROUT[6]), .DO7(ROUT[7]),
    .MC0(MC[0]), .MC1(MC[1]), .MC2(MC[2]), .MC3(MC[3]), .MC4(MC[4]), .MC5(MC[5]), .MC6(MC[6]), .MC7(MC[7]),
    .CLK(and_2_out), .RST(or_2_out), .DI10(DI[10]), .DI11(DI[11]), .DI12(DI[12]), .DI13(DI[13]),
    .DI14(DI[14]), .DI15(DI[15]), .DI0(DI[0]), .DI1(DI[1]), .DI2(DI[2]), .DI3(DI[3]), .DI4(DI[4]),
    .DI5(DI[5]), .DI6(DI[6]), .DI7(DI[7]), .DI8(DI[8]), .DI9(DI[9]));
  not not_4 (not_4_out, LWE);
  Button button_1 (.out(button_1_out));
  Clock clock_1 (.out(clock_1_out));
  Button button_2 (.out(RST));
  Button button_3 (.out(RSTProc));
  assign controlled_buffer_2_out = LWE ? LWE : 1'bz;  // Controlled_Buffer controlled_buffer_3
  assign stsy = not_4_out ? neutroser_n1_1_sync : 1'bz;  // Controlled_Buffer controlled_buffer_4
  assign stsy = LWE ? ram_loader_1_sync : 1'bz;  // Controlled_Buffer controlled_buffer_5
  assign controlled_buffer_6_out = not_5_out ? ROUT : 16'bz;  // Controlled_Buffer controlled_buffer_6
  // Probe on ROUT
  or or_3 (CLK, button_1_out, clock_1_out);
  // Probe on controlled_buffer_1_out
  assign controlled_buffer_1_out = LWE ? ram_loader_1_mc : 8'bz;  // Controlled_Buffer controlled_buffer_7
  RAM #(.dataWidth(16), .trigger("falling")) ram_1 (
    .addr(controlled_buffer_1_out), .we(controlled_buffer_2_out), .clk(rsync), .din(controlled_buffer_6_out),
    .dout(DI));  // open: oe
  RAM_Loader ram_loader_1 (
    .DROM(rom_1_data), .CLK(CLK), .RST(RST), .MC(ram_loader_1_mc), .DOUT(ram_loader_1_dout),
    .SYNC(ram_loader_1_sync), .WE(LWE));
  not not_5 (not_5_out, LWE);
  assign controlled_buffer_6_out = LWE ? ram_loader_1_dout : 16'bz;  // Controlled_Buffer controlled_buffer_8
  // Probe on DI

  // Notes on the sheet:
  //   contents of rom_1 (hex, n*v repeats v):
  //   104 505 607 b06 4 4 0 2
  //   LOAD 01
  //   JUMP 02
  //   SUM 03
  //   SUB 04
  //   MUL 05
  //   DIV 06
  //   INV 07
  //   AND 08
  //   OR 09
  //   XOR 0a
  //   WRITE 0b
  //   CHANGE 0c
  //   SHR 0d
  //   SHL 0e
endmodule

module RAM_Loader (
  input  [15:0] DROM,
  input  CLK,
  input  RST,
  output [7:0] MC,
  output [15:0] DOUT,
  output SYNC,
  output WE
);

  and and_1 (SYNC, WE, CLK);
  Counter #(.trigger("falling")) counter_1 (.Q(MC), .clk(SYNC), .clr(RST));  // open: load, D, count, carry, up
  nand nand_1 (WE, MC[7], MC[6], MC[5], MC[4], MC[3], MC[2], MC[1], MC[0]);

  assign DOUT = DROM;
endmodule
